# Fritzing sketch Musicbox (saved by Fritzing 0.9.2b)

parts:
  Raspberry_Pi2 = Raspberry Pi B+
  R3 = Resistor [tolerance=±5% resistance=2.2k package=THT]
  RDM6300 = mystery part, 10 pins [chip_label=RDM6300]
  R4 = Rotary Potentiometer (Small) [maximum_resistance=100kΩ package=THT]
  U1 = mystery part, 8 pins [chip_label=MCP3202]
  LCD1 = LCD screen
  R5 = Resistor [tolerance=±5% resistance=560 package=THT]
  S2 = Square Pushbutton
  S3 = Square Pushbutton
  S4 = Square Pushbutton
  S5 = Square Pushbutton
  R7 = Resistor [tolerance=±5% resistance=4.7k package=THT]
  J1 = longpad pin header, 16 pins [form="long pad"]
  J2 = longpad pin header, 1 pin [form="long pad"]
  J3 = longpad pin header, 1 pin [form="long pad"]
  J4 = longpad pin header, 1 pin [form="long pad"]
  J5 = longpad pin header, 1 pin [form="long pad"]
  J6 = longpad pin header, 1 pin [form="long pad"]
  J7 = longpad pin header, 1 pin [form="long pad"]
  J9 = longpad pin header, 1 pin [form="long pad"]
  J10 = longpad pin header, 1 pin [form="long pad"]
  Power_plug1 = Power plug
  R8 = Resistor [tolerance=±5% resistance=10k package=THT]
  Q3 = NPN-Transistor [package="TO92 [THT]"]
  Q4 = NPN-Transistor [package="TO92 [THT]"]
  R9 = Resistor [tolerance=±5% resistance=100k package=THT]
  R10 = Resistor [tolerance=±5% resistance=180k package=THT]
  J11 = longpad pin header, 1 pin [form="long pad"]
  J12 = longpad pin header, 1 pin [form="long pad"]
  R11 = Resistor [tolerance=±5% resistance=10k package=THT]
  J13 = longpad pin header, 1 pin [form="long pad"]
  R12 = Resistor [tolerance=±5% resistance=4.7k package=THT]
  J14 = longpad pin header, 1 pin [form="long pad"]
  J15 = longpad pin header, 1 pin [form="long pad"]
  J16 = longpad pin header, 4 pins [form="long pad"]
  J17 = longpad pin header, 1 pin [form="long pad"]
  J18 = longpad pin header, 1 pin [form="long pad"]
  U2 = Optocoupler [package=THT]
  R13 = Resistor [tolerance=±5% resistance=220 package=THT]

nets:
  N1: Raspberry_Pi2.3v3, R4.leg1, U1.pin8, S2.leg1, S3.leg1, S4.leg1, J2.pin1, J3.pin1, J4.pin1
  N2: Raspberry_Pi2.GPIO2, J1.pin4
  N3: Raspberry_Pi2.GPIO3, J1.pin5
  N4: Raspberry_Pi2.GPIO4, Power_plug1.GND, Q3.E, Q4.E, R10.Pin_1, J12.pin1, R11.Pin_1
  N5: Raspberry_Pi2.GPIO17, J16.pin1
  N6: Raspberry_Pi2.GPIO27, J16.pin2
  N7: Raspberry_Pi2.GPIO10, U1.pin5
  N8: Raspberry_Pi2.GPIO9, U1.pin6
  N9: Raspberry_Pi2.GPIO11, U1.pin7
  N10: Raspberry_Pi2.GPIO6, LCD1.DB4
  N11: Raspberry_Pi2.GPIO13, LCD1.DB5
  N12: Raspberry_Pi2.GPIO19, LCD1.DB6
  N13: Raspberry_Pi2.GPIO26, LCD1.DB7
  N14: Raspberry_Pi2.GPIO21, LCD1.RS
  N15: Raspberry_Pi2.GPIO20, LCD1.E, LCD1.DB0
  N16: Raspberry_Pi2.GPIO16, R8.Pin_1
  GND: Raspberry_Pi2.GND, RDM6300.pin9, R4.leg2, U1.pin4, LCD1.VSS, LCD1.V0, LCD1.R/W, LCD1.LED-, R7.Pin_1, J5.pin1, J6.pin1, J9.pin1, U2.Pin_2
  N17: Raspberry_Pi2.GPIO12, R13.Pin_1
  N18: Raspberry_Pi2.GPIO8, U1.pin1
  N19: Raspberry_Pi2.GPIO24, S4.leg0
  N20: Raspberry_Pi2.GPIO23, S3.leg0
  N21: Raspberry_Pi2.GPIO18, S2.leg0
  N22: Raspberry_Pi2.GPIO15, R3.Pin_0, R7.Pin_0
  5V: Raspberry_Pi2.5V, RDM6300.pin10, LCD1.VDD, R5.Pin_0, J7.pin1, J10.pin1, Power_plug1.VCC, R9.Pin_1, R12.Pin_1, J15.pin1
  N23: R3.Pin_1, RDM6300.pin1
  N24: R4.wiper, U1.pin2, U1.pin3
  N25: LCD1.LED+, R5.Pin_1
  N26: S5.leg0, J16.pin4, J18.pin1, U2.Pin_4
  N27: S5.leg1, J16.pin3, J17.pin1, U2.Pin_5
  N28: J1.pin7, Q4.C, R9.Pin_0, R10.Pin_0, J11.pin1
  N29: R8.Pin_0, Q3.B, R11.Pin_0, J13.pin1
  N30: Q3.C, Q4.B, R12.Pin_0, J14.pin1
  N31: U2.Pin_1, R13.Pin_0

notes:
  Amp MAX9744
  Play/Pause
  Prev Track
  Next Track
  Power
  PiATX
  Standby Schaltung für AMP
  Optokoppler
  RFID RDM6300
  Lautstärken Poti
  MCP 3202
  A/D Wandler
  HD44780
